// Logisim project Group 3 - Traffic Light 2021.circ as structural Verilog: 7 circuits, main circuit main
module main (
);

  wire and_1_out, clock_1_out, n74138_1_y0, n74138_1_y1, n74138_1_y2, n74138_1_y3, n74138_1_y4, n74138_1_y5,
       n74138_1_y6, n74138_1_y7, n74139_1_y0, n74139_1_y1, n74139_1_y2, n74139_2_y0, n74139_2_y1,
       n74139_2_y2, n74139_3_y0, n74139_3_y1, n74139_3_y2, n74139_4_y0, n74139_4_y1, n74139_4_y2, n74151_1_y,
       n74151_2_y, n74151_3_y, n74175_1_q4, n74193_1_not_tg, n74193_1_q0, not_1_out, not_2_out;
  wire [2:0] n74175_1_q1;

  Clock clock_1 (.out(clock_1_out));
  _74193 u_74193_1 (
    .Load(1'b1), .Up(clock_1_out), .Dn(1'b1), .Clr(n74175_1_q4), .Not_TG(n74193_1_not_tg), .Q0(n74193_1_q0));  // open: TA, Q1, Q2, Q3
  and and_1 (and_1_out, n74193_1_q0, n74175_1_q1[0]);
  _74175 u_74175_1 (
    .D1(n74151_1_y), .Q1(n74175_1_q1[0]), .D2(n74151_2_y), .Q2(n74175_1_q1[1]), .D3(n74151_3_y),
    .Q3(n74175_1_q1[2]), .D4(and_1_out), .Q4(n74175_1_q4), .CLK(clock_1_out), .CLR(1'b1));
  LED led_1 (.in(n74139_1_y2));
  LED led_2 (.in(n74139_1_y1));
  LED led_3 (.in(n74139_1_y0));
  _74139 u_74139_1 (
    .A0(n74138_1_y7), .A1(n74138_1_y6), .Y0(n74139_1_y0), .Y1(n74139_1_y1), .Y2(n74139_1_y2));  // open: Y3
  not not_1 (not_1_out, n74193_1_not_tg);
  LED led_4 (.in(n74139_2_y0));
  _74139 u_74139_2 (
    .A0(n74138_1_y1), .A1(n74138_1_y0), .Y0(n74139_2_y0), .Y1(n74139_2_y1), .Y2(n74139_2_y2));  // open: Y3
  LED led_5 (.in(n74139_3_y2));
  not not_2 (not_2_out, n74193_1_q0);
  LED led_6 (.in(n74139_2_y2));
  LED led_7 (.in(n74139_2_y1));
  _74138 u_74138_1 (
    .A0(n74175_1_q1[0]), .A1(n74175_1_q1[1]), .A2(n74175_1_q1[2]), .Y0(n74138_1_y0), .Y1(n74138_1_y1),
    .Y2(n74138_1_y2), .Y3(n74138_1_y3), .Y4(n74138_1_y4), .Y5(n74138_1_y5), .Y6(n74138_1_y6), .Y7(n74138_1_y7));
  _74139 u_74139_3 (
    .A0(n74138_1_y5), .A1(n74138_1_y4), .Y0(n74139_3_y0), .Y1(n74139_3_y1), .Y2(n74139_3_y2));  // open: Y3
  LED led_8 (.in(n74139_3_y1));
  LED led_9 (.in(n74139_3_y0));
  _74139 u_74139_4 (
    .A0(n74138_1_y3), .A1(n74138_1_y2), .Y0(n74139_4_y0), .Y1(n74139_4_y1), .Y2(n74139_4_y2));  // open: Y3
  LED led_10 (.in(n74139_4_y0));
  LED led_11 (.in(n74139_4_y1));
  LED led_12 (.in(n74139_4_y2));
  _74151 u_74151_1 (
    .A(not_1_out), .B(not_2_out), .C(not_1_out), .D(not_2_out), .E(not_1_out), .F(not_2_out), .G(not_1_out),
    .J(not_2_out), .Y(n74151_1_y), .S0(n74175_1_q1[0]), .S1(n74175_1_q1[1]), .S2(n74175_1_q1[2]));  // open: OE
  _74151 u_74151_2 (
    .A(1'b0), .B(n74193_1_q0), .C(1'b1), .D(not_2_out), .E(1'b0), .F(n74193_1_q0), .G(1'b1), .J(not_2_out),
    .Y(n74151_2_y), .S0(n74175_1_q1[0]), .S1(n74175_1_q1[1]), .S2(n74175_1_q1[2]));  // open: OE
  _74151 u_74151_3 (
    .A(1'b0), .B(1'b0), .C(1'b0), .D(n74193_1_q0), .E(1'b1), .F(1'b1), .G(1'b1), .J(not_2_out),
    .Y(n74151_3_y), .S0(n74175_1_q1[0]), .S1(n74175_1_q1[1]), .S2(n74175_1_q1[2]));  // open: OE
endmodule

module _74175 (
  input  CLK,
  input  D1,
  input  D2,
  input  D3,
  input  D4,
  input  CLR,
  output Q1,
  output Q2,
  output Q3,
  output Q4
);

  wire not_1_out;

  D_Flip_Flop d_flip_flop_1 (.D(D1), .CLK(CLK), .Q(Q1), .CLR(not_1_out));  // open: SET
  D_Flip_Flop d_flip_flop_2 (.D(D2), .CLK(CLK), .Q(Q2), .CLR(not_1_out));  // open: SET
  D_Flip_Flop d_flip_flop_3 (.D(D3), .CLK(CLK), .Q(Q3), .CLR(not_1_out));  // open: SET
  D_Flip_Flop d_flip_flop_4 (.D(D4), .CLK(CLK), .Q(Q4), .CLR(not_1_out));  // open: SET
  not not_1 (not_1_out, CLR);
endmodule

module _74193 (
  input  Load,
  input  Up,
  input  Dn,
  input  Clr,
  output Not_TG,
  output TA,
  output Q0,
  output Q1,
  output Q2,
  output Q3
);

  wire and_1_out, and_2_out, and_3_out, and_4_out, and_5_out, and_6_out, buffer_1_out, buffer_2_out,
       nand_1_out, nand_2_out, nand_3_out, nand_4_out, nand_5_out, nand_6_out, nand_7_out, nand_8_out,
       nand_9_out, nand_10_out, nor_1_out, nor_2_out, nor_3_out, nor_4_out, not_1_out, not_2_out, not_3_out,
       not_4_out, not_5_out, not_6_out, not_7_out, not_8_out, or_1_out, or_2_out, or_3_out, or_4_out,
       t_ff_1_q, t_ff_1_qn, t_ff_2_q, t_ff_2_qn, t_ff_3_q, t_ff_3_qn, t_ff_4_q, t_ff_4_qn;

  not not_1 (not_1_out, Load);
  not not_2 (not_2_out, Up);
  buf buffer_1 (buffer_1_out, not_2_out);
  buf buffer_2 (buffer_2_out, not_3_out);
  not not_3 (not_3_out, Dn);
  not not_4 (not_4_out, Clr);
  nand nand_1 (nand_1_out, not_1_out, not_4_out);
  not not_5 (not_5_out, nand_1_out);
  nor nor_1 (nor_1_out, buffer_1_out, buffer_2_out);
  or or_1 (or_1_out, ~not_4_out, ~nand_2_out);  // OR_Gate
  nand nand_2 (nand_2_out, nand_1_out, not_1_out);
  T_Flip_Flop t_ff_1 (
    .clk(nor_1_out), .T(nor_1_out), .Q(t_ff_1_q), .Qn(t_ff_1_qn), .preset(not_5_out), .reset(or_1_out));  // open: en
  buf buffer_3 (Q0, t_ff_1_q);
  and and_1 (and_1_out, not_2_out, t_ff_1_q);
  nor nor_2 (nor_2_out, and_1_out, and_2_out);
  and and_2 (and_2_out, t_ff_1_qn, not_3_out);
  nand nand_3 (nand_3_out, nand_4_out, not_1_out);
  nand nand_4 (nand_4_out, not_1_out, not_4_out);
  not not_6 (not_6_out, nand_4_out);
  T_Flip_Flop t_ff_2 (
    .clk(nor_2_out), .T(nor_2_out), .Q(t_ff_2_q), .Qn(t_ff_2_qn), .preset(not_6_out), .reset(or_2_out));  // open: en
  or or_2 (or_2_out, ~not_4_out, ~nand_3_out);  // OR_Gate
  buf buffer_4 (Q1, t_ff_2_q);
  and and_3 (and_3_out, not_2_out, t_ff_1_q, t_ff_2_q);
  and and_4 (and_4_out, t_ff_2_qn, t_ff_1_qn, not_3_out);
  nor nor_3 (nor_3_out, and_3_out, and_4_out);
  nand nand_5 (nand_5_out, nand_6_out, not_1_out);
  nand nand_6 (nand_6_out, not_1_out, not_4_out);
  not not_7 (not_7_out, nand_6_out);
  T_Flip_Flop t_ff_3 (
    .clk(nor_3_out), .T(nor_3_out), .Q(t_ff_3_q), .Qn(t_ff_3_qn), .preset(not_7_out), .reset(or_3_out));  // open: en
  or or_3 (or_3_out, ~not_4_out, ~nand_5_out);  // OR_Gate
  buf buffer_5 (Q2, t_ff_3_q);
  and and_5 (and_5_out, t_ff_2_q, not_2_out, t_ff_1_q, t_ff_3_q);
  nor nor_4 (nor_4_out, and_5_out, and_6_out);
  and and_6 (and_6_out, t_ff_3_qn, t_ff_2_qn, t_ff_1_qn, not_3_out);
  nand nand_7 (nand_7_out, nand_8_out, not_1_out);
  nand nand_8 (nand_8_out, not_1_out, not_4_out);
  not not_8 (not_8_out, nand_8_out);
  T_Flip_Flop t_ff_4 (
    .clk(nor_4_out), .T(nor_4_out), .Q(t_ff_4_q), .Qn(t_ff_4_qn), .preset(not_8_out), .reset(or_4_out));  // open: en
  or or_4 (or_4_out, ~not_4_out, ~nand_7_out);  // OR_Gate
  buf buffer_6 (Q3, t_ff_4_q);
  nand nand_9 (nand_9_out, t_ff_3_q, not_2_out, t_ff_4_q, t_ff_2_q, t_ff_1_q);
  nand nand_10 (nand_10_out, t_ff_1_qn, t_ff_4_qn, t_ff_3_qn, t_ff_2_qn, not_3_out);
  buf buffer_7 (Not_TG, nand_9_out);
  buf buffer_8 (TA, nand_10_out);
endmodule

module _74151 (
  input  S0,
  input  S1,
  input  S2,
  input  A,
  input  B,
  input  C,
  input  D,
  input  E,
  input  F,
  input  G,
  input  J,
  input  OE,
  output Y
);

  wire and_1_out, and_2_out, and_3_out, and_4_out, and_5_out, and_6_out, and_7_out, and_8_out, not_1_out,
       not_2_out, not_3_out, not_4_out;

  not not_1 (not_1_out, S0);
  not not_2 (not_2_out, S1);
  not not_3 (not_3_out, OE);
  not not_4 (not_4_out, S2);
  and and_1 (and_1_out, A, not_1_out, not_2_out, not_4_out);
  and and_2 (and_2_out, B, S0, not_2_out, not_4_out);
  and and_3 (and_3_out, C, not_1_out, S1, not_4_out);
  and and_4 (and_4_out, D, S0, S1, not_4_out);
  and and_5 (and_5_out, E, not_1_out, not_2_out, S2);
  and and_6 (and_6_out, F, S0, not_2_out, S2);
  and and_7 (and_7_out, G, not_1_out, S1, S2);
  and and_8 (and_8_out, J, S0, S1, S2);
  or or_1 (Y, and_1_out, and_2_out, and_3_out, and_4_out, and_5_out, and_6_out, and_7_out, and_8_out);
endmodule

module D_Flip_Flop (
  input  SET,
  input  D,
  input  CLK,
  input  CLR,
  output Q
);

  D_Flip_Flop_part d_ff_1 (.clk(CLK), .D(D), .Q(Q), .preset(SET), .reset(CLR));  // open: Qn, en
endmodule

module _74139 (
  input  A0,
  input  A1,
  output Y0,
  output Y1,
  output Y2,
  output Y3
);

  wire not_1_out, not_2_out;

  not not_1 (not_1_out, A0);
  not not_2 (not_2_out, A1);
  and and_1 (Y0, not_1_out, not_2_out);
  and and_2 (Y1, A0, not_2_out);
  and and_3 (Y2, not_1_out, A1);
  and and_4 (Y3, A0, A1);
endmodule

module _74138 (
  input  A0,
  input  A1,
  input  A2,
  output Y0,
  output Y1,
  output Y2,
  output Y3,
  output Y4,
  output Y5,
  output Y6,
  output Y7
);

  wire not_1_out, not_2_out, not_3_out;

  not not_1 (not_1_out, A0);
  not not_2 (not_2_out, A1);
  not not_3 (not_3_out, A2);
  and and_1 (Y0, not_1_out, not_2_out, not_3_out);
  and and_2 (Y1, A0, not_2_out, not_3_out);
  and and_3 (Y2, not_1_out, A1, not_3_out);
  and and_4 (Y3, A0, A1, not_3_out);
  and and_5 (Y4, not_1_out, not_2_out, A2);
  and and_6 (Y5, A0, not_2_out, A2);
  and and_7 (Y6, not_1_out, A1, A2);
  and and_8 (Y7, A0, A1, A2);
endmodule
